# Fritzing sketch hack-switch-make-smart (saved by Fritzing 0.9.9b)
breadboards: 1

parts:
  2N2222 = NPN-Transistor [package="TO92 [THT]"]
  S1 = Pushbutton [package="[THT]"]
  R1 = Resistor [tolerance=±5% power=0.25 resistance=220 package=THT]

nets:
  N1: 2N2222.E, S1.Pin_1, S1.Pin_2
  N2: 2N2222.B, R1.Pin_1
  N3: 2N2222.C, S1.Pin_3, S1.Pin_4
  GPIO: R1.Pin_0

notes:
  External switch
  GPIO
